// Logisim project bit4_Data_Selector0.circ as structural Verilog: 1 circuit, main circuit main
module main (
);

  wire undriven_3;
  wire [3:0] multiplexer_1_out, undriven, undriven_2;

  Multiplexer multiplexer_1 (
    .in0(undriven_2[0]), .in1(undriven[0]), .out(multiplexer_1_out[0]), .sel(undriven_3));  // open: en
  Multiplexer multiplexer_2 (
    .in0(undriven_2[1]), .in1(undriven[1]), .out(multiplexer_1_out[1]), .sel(undriven_3));  // open: en
  Multiplexer multiplexer_3 (
    .in0(undriven_2[2]), .in1(undriven[2]), .out(multiplexer_1_out[2]), .sel(undriven_3));  // open: en
  Multiplexer multiplexer_4 (
    .in0(undriven_2[3]), .in1(undriven[3]), .out(multiplexer_1_out[3]), .sel(undriven_3));  // open: en
endmodule
