// Logisim project bit8_ABreg0_ALU0.circ as structural Verilog: 1 circuit, main circuit main
module main (
  input  [7:0] in_1,
  input  in_2,
  input  [7:0] in_3,
  input  in_4,
  output [7:0] out_5
);

  wire [7:0] register_1_q, register_2_q, xor_1_out;

  Register register_1 (.D(in_1), .en(1'b1), .Q(register_1_q), .clk(in_2), .clr(1'b0));
  Register register_2 (.D(in_3), .en(1'b1), .Q(register_2_q), .clk(in_2), .clr(1'b0));
  // Probe on register_1_q
  // Probe on register_2_q
  Adder adder_1 (.a(register_1_q), .b(xor_1_out), .out(out_5), .cin(in_4));  // open: cout
  // Probe on xor_1_out[0]
  xor xor_1 (xor_1_out[0], register_2_q[0], in_4);
  xor xor_2 (xor_1_out[1], register_2_q[1], in_4);
  // Probe on xor_1_out[1]
  // Probe on xor_1_out[2]
  xor xor_3 (xor_1_out[2], register_2_q[2], in_4);
  xor xor_4 (xor_1_out[3], register_2_q[3], in_4);
  // Probe on xor_1_out[3]
  xor xor_5 (xor_1_out[4], register_2_q[4], in_4);
  // Probe on xor_1_out[4]
  xor xor_6 (xor_1_out[5], register_2_q[5], in_4);
  // Probe on xor_1_out[5]
  xor xor_7 (xor_1_out[6], register_2_q[6], in_4);
  // Probe on xor_1_out[6]
  xor xor_8 (xor_1_out[7], register_2_q[7], in_4);
  // Probe on xor_1_out[7]
  // Probe on out_5
  // also tied to GND on the sheet: in_4

  // Notes on the sheet:
  //   Subtract
endmodule
