// Logisim project bit8_ALU0.circ as structural Verilog: 1 circuit, main circuit 8bit ALU
// e
module _8bit_ALU (
  input  [7:0] A,
  input  EO,
  input  [7:0] B,
  input  S,
  output [7:0] out_5,
  output [7:0] E
);

  wire [7:0] xor_1_out;

  Adder adder_1 (.a(A), .b(xor_1_out), .out(out_5), .cin(S));  // open: cout
  xor xor_1 (xor_1_out[0], B[0], S);
  // Probe on xor_1_out[0]
  // Probe on xor_1_out[1]
  xor xor_2 (xor_1_out[1], B[1], S);
  xor xor_3 (xor_1_out[2], B[2], S);
  // Probe on xor_1_out[2]
  // Probe on xor_1_out[3]
  xor xor_4 (xor_1_out[3], B[3], S);
  // Probe on xor_1_out[4]
  xor xor_5 (xor_1_out[4], B[4], S);
  xor xor_6 (xor_1_out[5], B[5], S);
  // Probe on xor_1_out[5]
  // Probe on xor_1_out[6]
  xor xor_7 (xor_1_out[6], B[6], S);
  // Probe on xor_1_out[7]
  xor xor_8 (xor_1_out[7], B[7], S);
  assign E[0] = EO ? out_5[0] : 1'bz;  // Controlled_Buffer controlled_buffer_1
  assign E[1] = EO ? out_5[1] : 1'bz;  // Controlled_Buffer controlled_buffer_2
  assign E[2] = EO ? out_5[2] : 1'bz;  // Controlled_Buffer controlled_buffer_3
  assign E[3] = EO ? out_5[3] : 1'bz;  // Controlled_Buffer controlled_buffer_4
  assign E[4] = EO ? out_5[4] : 1'bz;  // Controlled_Buffer controlled_buffer_5
  assign E[5] = EO ? out_5[5] : 1'bz;  // Controlled_Buffer controlled_buffer_6
  assign E[6] = EO ? out_5[6] : 1'bz;  // Controlled_Buffer controlled_buffer_7
  assign E[7] = EO ? out_5[7] : 1'bz;  // Controlled_Buffer controlled_buffer_8

  // Notes on the sheet:
  //   2's compliment
endmodule
