// Logisim project bit8_computer0.circ as structural Verilog: 1 circuit, main circuit bit8 Computer
module bit8_Computer (
);

  wire clock_1_out, clock_2_out, clock_3_out, clock_4_out, clock_5_out, clock_6_out, clock_7_out,
       clock_8_out, not_1_out, pull_resistor_2_node;
  wire [0:0] rom_2_data_2;
  wire [3:0] adder_1_out, bit_4register_1_out_5, controlled_buffer_1_out_2, counter_1_q, counter_2_q,
       n8bit_register_1_q, register_1_q, undriven;
  wire [7:0] A_q, ALU_e, ALU_out_5, B_q, ram_1_data, rom_1_data;
  wire [7:4] controlled_buffer_1_out;
  wire [11:0] rom_2_data;

  not not_1 (not_1_out, rom_2_data_2[0]);
  Pull_Resistor #(.pull(1)) pull_resistor_1 (.node(not_1_out));
  Counter #(.width(4), .max('h3)) counter_1 (
    .load(1'b0), .count(not_1_out), .Q(counter_1_q), .clk(clock_1_out), .clr(1'b0));  // open: D, carry
  Clock clock_1 (.out(clock_1_out));
  Clock clock_2 (.out(clock_2_out));
  Pull_Resistor #(.pull(1)) pull_resistor_2 (.node(pull_resistor_2_node));
  bit_4Register bit_4register_1 (
    .Q(controlled_buffer_1_out_2), .out_5(bit_4register_1_out_5), .CLK(clock_2_out), .RI(rom_2_data[3]),
    .RO(1'b1));
  Register #(.width(4)) register_1 (.D(n8bit_register_1_q), .Q(register_1_q), .clk(clock_3_out));  // open: en, clr
  Clock clock_3 (.out(clock_3_out));
  // Probe on bit_4register_1_out_5
  RAM #(.addrWidth(4)) ram_1 (
    .addr(bit_4register_1_out_5), .data(ram_1_data), .sel(1'b1), .clk(clock_4_out), .clr(1'b0));  // open: ld
  Clock clock_4 (.out(clock_4_out));
  Clock clock_5 (.out(clock_5_out));
  Adder #(.width(4)) adder_1 (.a(register_1_q), .b({3'b000, rom_2_data_2[0]}), .out(adder_1_out));  // open: cin, cout
  ROM #(.addrWidth(3)) rom_1 (.addr({1'b0, counter_1_q[1:0]}), .data(rom_1_data), .sel(pull_resistor_2_node));
  assign {controlled_buffer_1_out, controlled_buffer_1_out_2} = rom_2_data[4] ? ram_1_data : 8'bz;  // Controlled_Buffer controlled_buffer_1
  _8bit_Register u_8bit_register_1 (
    .D({controlled_buffer_1_out, controlled_buffer_1_out_2}), .clock(clock_5_out), .RI(rom_2_data[6]),
    .RO(rom_2_data[5]), .Q({n8bit_register_1_q, controlled_buffer_1_out_2}));
  // Probe on {n8bit_register_1_q, controlled_buffer_1_out_2}
  ROM #(.addrWidth(4), .dataWidth(13)) rom_2 (
    .addr(adder_1_out), .data({rom_2_data_2[0], rom_2_data}), .sel(rom_1_data[6]));
  assign rom_2_data[6] = rom_1_data[7] ? rom_1_data[5] : 1'bz;  // Controlled_Buffer controlled_buffer_2
  // Probe on {controlled_buffer_1_out, controlled_buffer_1_out_2}
  Pull_Resistor pull_resistor_3 (.node({rom_2_data_2[0], rom_2_data}));
  assign rom_2_data[4] = rom_1_data[7] ? rom_1_data[3] : 1'bz;  // Controlled_Buffer controlled_buffer_3
  assign rom_2_data[5] = rom_1_data[7] ? rom_1_data[4] : 1'bz;  // Controlled_Buffer controlled_buffer_4
  assign rom_2_data[3] = rom_1_data[7] ? rom_1_data[2] : 1'bz;  // Controlled_Buffer controlled_buffer_5
  Clock clock_6 (.out(clock_6_out));
  Clock clock_7 (.out(clock_7_out));
  assign rom_2_data[1] = rom_1_data[7] ? rom_1_data[1] : 1'bz;  // Controlled_Buffer controlled_buffer_6
  assign rom_2_data[0] = rom_1_data[7] ? rom_1_data[0] : 1'bz;  // Controlled_Buffer controlled_buffer_7
  Counter #(.width(4), .max('hf)) counter_2 (
    .load(1'b0), .D(undriven), .count(rom_2_data[1]), .Q(counter_2_q), .clk(clock_8_out), .clr(rom_2_data[2]));  // open: carry
  Clock clock_8 (.out(clock_8_out));
  _8bit_Register A (
    .D({controlled_buffer_1_out, controlled_buffer_1_out_2}), .clock(clock_6_out), .RI(rom_2_data[8]),
    .RO(rom_2_data[7]), .Q(A_q));
  _8bit_Register B (
    .D({controlled_buffer_1_out, controlled_buffer_1_out_2}), .clock(clock_6_out), .RI(rom_2_data[10]),
    .RO(rom_2_data[9]), .Q(B_q));
  _8bit_Register u_8bit_register_2 (
    .D(ALU_e), .clock(clock_7_out), .RI(1'b1), .RO(rom_2_data[11]),
    .Q({controlled_buffer_1_out, controlled_buffer_1_out_2}));
  assign controlled_buffer_1_out_2 = rom_2_data[0] ? counter_2_q : 4'bz;  // Controlled_Buffer controlled_buffer_8
  // Probe on A_q
  // Probe on ALU_out_5
  _8bit_ALU ALU (.A(A_q), .B(B_q), .E(ALU_e), .S(1'b0), .EO(rom_2_data[11]), .out_5(ALU_out_5));
  // Probe on B_q
  // Probe on controlled_buffer_1_out_2

  // Notes on the sheet:
  //   CsE
  //   R
  //   MAR
  //   MI
  //   MO
  //   RAM
  //   IR
  //   II
  //   CONTROL LOGIC
  //   contents of rom_1 (hex, n*v repeats v):
  //   85 a8 94 40
  //   RO
  //   IO
  //   contents of rom_2 (hex, n*v repeats v):
  //   112 412 1a80 902
  //   CI
  //   CmE
  //   BUS
  //   BI
  //   COUNTER
  //   R
  //   AI
  //   AO
  //   S
  //   BO
  //   DISPR
  //   CO
  //   EO
endmodule
