// Logisim project bit8_computer1.circ as structural Verilog: 1 circuit, main circuit bit8_computer1
module bit8_computer1 (
);

  wire clock_1_out, clock_2_out, clock_3_out, clock_4_out, clock_5_out, clock_6_out, clock_7_out,
       clock_8_out, not_1_out;
  wire [3:0] bit_4register_1_out_5, controlled_buffer_1_out, controlled_buffer_3_out_2, counter_1_q,
       counter_2_q, pull_resistor_1_node, register_1_q, undriven;
  wire [7:0] n8bit_alu_1_e, n8bit_alu_1_out_5, n8bit_register_2_q, n8bit_register_3_q, ram_1_data;
  wire [7:4] controlled_buffer_3_out;
  wire [15:0] rom_1_data;

  Clock clock_1 (.out(clock_1_out));
  Clock clock_2 (.out(clock_2_out));
  assign controlled_buffer_1_out = not_1_out ? register_1_q : 4'bz;  // Controlled_Buffer controlled_buffer_1
  Register #(.width(4)) register_1 (.D(pull_resistor_1_node), .Q(register_1_q), .clk(clock_1_out));  // open: en, clr
  not not_1 (not_1_out, rom_1_data[12]);
  assign controlled_buffer_1_out = rom_1_data[12] ? counter_1_q : 4'bz;  // Controlled_Buffer controlled_buffer_2
  Counter #(.width(4), .max('hf)) counter_1 (
    .count(rom_1_data[12]), .Q(counter_1_q), .clk(clock_2_out), .clr(rom_1_data[13]));  // open: load, D, carry
  Clock clock_3 (.out(clock_3_out));
  Clock clock_4 (.out(clock_4_out));
  Clock clock_5 (.out(clock_5_out));
  Pull_Resistor pull_resistor_1 (.node(pull_resistor_1_node));
  ROM #(.addrWidth(4), .dataWidth(16)) rom_1 (.addr(controlled_buffer_1_out), .data(rom_1_data));  // open: sel
  bit_4Register bit_4register_1 (
    .Q(controlled_buffer_3_out_2), .out_5(bit_4register_1_out_5), .CLK(clock_3_out), .RI(rom_1_data[3]),
    .RO(1'b1));
  assign {controlled_buffer_3_out, controlled_buffer_3_out_2} = rom_1_data[4] ? ram_1_data : 8'bz;  // Controlled_Buffer controlled_buffer_3
  RAM #(.addrWidth(4)) ram_1 (
    .addr(bit_4register_1_out_5), .data(ram_1_data), .sel(1'b1), .clk(clock_4_out), .clr(1'b0));  // open: ld
  _8bit_Register u_8bit_register_1 (
    .D({controlled_buffer_3_out, controlled_buffer_3_out_2}), .clock(clock_5_out), .RI(rom_1_data[6]),
    .RO(rom_1_data[5]), .Q({pull_resistor_1_node, controlled_buffer_3_out_2}));
  Pull_Resistor pull_resistor_2 (.node(rom_1_data));
  // Probe on {controlled_buffer_3_out, controlled_buffer_3_out_2}
  // Probe on rom_1_data
  Clock clock_6 (.out(clock_6_out));
  Counter #(.width(4), .max('hf)) counter_2 (
    .load(1'b0), .D(undriven), .count(rom_1_data[1]), .Q(counter_2_q), .clk(clock_7_out), .clr(rom_1_data[2]));  // open: carry
  Clock clock_7 (.out(clock_7_out));
  // Probe on n8bit_register_2_q
  _8bit_Register u_8bit_register_2 (
    .D({controlled_buffer_3_out, controlled_buffer_3_out_2}), .clock(clock_6_out), .RI(rom_1_data[8]),
    .RO(rom_1_data[7]), .Q(n8bit_register_2_q));
  _8bit_Register u_8bit_register_3 (
    .D({controlled_buffer_3_out, controlled_buffer_3_out_2}), .clock(clock_6_out), .RI(rom_1_data[10]),
    .RO(rom_1_data[9]), .Q(n8bit_register_3_q));
  // Probe on n8bit_register_3_q
  Clock clock_8 (.out(clock_8_out));
  // Probe on controlled_buffer_3_out_2
  assign controlled_buffer_3_out_2 = rom_1_data[0] ? counter_2_q : 4'bz;  // Controlled_Buffer controlled_buffer_4
  // Probe on n8bit_alu_1_out_5
  _8bit_ALU u_8bit_alu_1 (
    .A(n8bit_register_2_q), .B(n8bit_register_3_q), .E(n8bit_alu_1_e), .S(1'b0), .EO(rom_1_data[11]),
    .out_5(n8bit_alu_1_out_5));
  _8bit_Register u_8bit_register_4 (
    .D(n8bit_alu_1_e), .clock(clock_8_out), .RI(1'b1), .RO(rom_1_data[14]),
    .Q({controlled_buffer_3_out, controlled_buffer_3_out_2}));

  // Notes on the sheet:
  //   CONTROL LOGIC
  //   MAR
  //   MI
  //   RAM
  //   II
  //   contents of rom_1 (hex, n*v repeats v):
  //   1009 1050 1028 2112 2412 2a82 6102
  //   MO
  //   RO
  //   IR
  //   IO
  //   BUS
  //   CONTROL BITS
  //   CI
  //   CmE
  //   REG A
  //   AI
  //   REG B
  //   BI
  //   COUNTER
  //   R
  //   AO
  //   S
  //   BO
  //   DISPR
  //   CO
  //   ALU
  //   EO
  //   DO
endmodule
